// Logisim project seven_segment_disp.circ as structural Verilog
module seven_segment (
  input  in_1,
  output a,
  output b,
  output c,
  output d,
  output e,
  output f,
  output g
);

  wire and_1_out, and_2_out, and_3_out, and_4_out, and_5_out, and_6_out, and_7_out, and_8_out, and_9_out,
       and_10_out, and_11_out, and_12_out, and_13_out, and_14_out, and_15_out, and_16_out, counter_1_p1,
       counter_1_p3, counter_1_p4, counter_2_p1, counter_3_p1, not_1_out, not_2_out, not_3_out, not_4_out,
       not_5_out, not_6_out, not_7_out, not_8_out, not_9_out, not_10_out, not_11_out, not_12_out, not_13_out,
       not_14_out, not_15_out, not_16_out, not_17_out, not_18_out, not_19_out, not_20_out, not_21_out,
       not_22_out, not_23_out, not_24_out, not_25_out;

  // Counter #(.width(1), .max('h1)) counter_1: pin names not known; wires that end beside it: counter_1_p1, counter_1_p1, counter_1_p3, counter_1_p4
  // Counter #(.width(1), .max('h1)) counter_2: pin names not known; wires that end beside it: counter_2_p1, counter_1_p3
  // Counter #(.width(1), .max('h1)) counter_3: pin names not known; wires that end beside it: counter_3_p1, counter_2_p1
  // Counter #(.width(1), .max('h1)) counter_4: pin names not known; wires that end beside it: in_1, counter_3_p1
  not not_1 (not_1_out, counter_1_p4);
  not not_2 (not_2_out, counter_1_p3);
  not not_3 (not_3_out, counter_2_p1);
  not not_4 (not_4_out, counter_3_p1);
  not not_5 (not_5_out, not_2_out);
  not not_6 (not_6_out, not_4_out);
  not not_7 (not_7_out, not_3_out);
  not not_8 (not_8_out, not_4_out);
  not not_9 (not_9_out, not_3_out);
  not not_10 (not_10_out, not_2_out);
  not not_11 (not_11_out, not_4_out);
  not not_12 (not_12_out, not_2_out);
  not not_13 (not_13_out, not_4_out);
  not not_14 (not_14_out, not_3_out);
  not not_15 (not_15_out, not_2_out);
  not not_16 (not_16_out, not_4_out);
  not not_17 (not_17_out, not_4_out);
  not not_18 (not_18_out, not_3_out);
  not not_19 (not_19_out, not_4_out);
  not not_20 (not_20_out, not_3_out);
  not not_21 (not_21_out, not_4_out);
  not not_22 (not_22_out, not_2_out);
  not not_23 (not_23_out, not_3_out);
  not not_24 (not_24_out, not_4_out);
  and and_1 (and_1_out, not_5_out, not_6_out);
  and and_2 (and_2_out, not_2_out, not_4_out);
  not not_25 (not_25_out, not_2_out);
  and and_3 (and_3_out, not_7_out, not_8_out);
  and and_4 (and_4_out, not_3_out, not_4_out);
  or or_1 (c, not_9_out, not_4_out, not_2_out);
  and and_5 (and_5_out, not_10_out, not_11_out);
  and and_6 (and_6_out, not_12_out, not_3_out);
  and and_7 (and_7_out, not_3_out, not_13_out);
  and and_8 (and_8_out, not_2_out, not_14_out, not_4_out);
  and and_9 (and_9_out, not_15_out, not_16_out);
  and and_10 (and_10_out, not_3_out, not_17_out);
  and and_11 (and_11_out, not_18_out, not_19_out);
  and and_12 (and_12_out, not_2_out, not_20_out);
  and and_13 (and_13_out, not_2_out, not_21_out);
  and and_14 (and_14_out, not_22_out, not_3_out);
  and and_15 (and_15_out, not_2_out, not_23_out);
  and and_16 (and_16_out, not_2_out, not_24_out);
  or or_2 (a, and_1_out, not_3_out, and_2_out, not_1_out);
  or or_3 (b, not_25_out, and_3_out, and_4_out);
  or or_4 (d, and_5_out, and_6_out, and_7_out, and_8_out, not_1_out);
  or or_5 (e, and_9_out, and_10_out);
  or or_6 (f, and_11_out, and_12_out, and_13_out, not_1_out);
  or or_7 (g, and_14_out, and_15_out, and_16_out, not_1_out);
  _7_Segment_Display u_7_segment_display_1 (.g(g), .f(f), .a(a), .b(b), .e(e), .d(d), .c(c));  // open: dp
endmodule
